# Fritzing sketch breadboard_fritz copy (saved by Fritzing 1.0.1rc)
breadboards: 1

parts:
  Teensy++1 = Teensy 3.1  # not connected
  R1 = Rotary Potentiometer (Large) [maximum_resistance=100kΩ knob_status=50% power=0.5W package=THT]
  R2 = Rotary Potentiometer (Large) [maximum_resistance=100kΩ knob_status=50% power=0.5W package=THT]
  R3 = Rotary Potentiometer (Large) [maximum_resistance=100kΩ knob_status=50% power=0.5W package=THT]
  R4 = Rotary Potentiometer (Large) [maximum_resistance=100kΩ knob_status=50% power=0.5W package=THT]
  S3 = Momentary Switch [package=ksa_sealed_tac_switch]
  S4 = Toggle Switch [package=THT]

nets:
  N1: R1.leg1, R2.leg1, R3.leg1, R4.leg1, S3.4, S4.L1
  N2: R1.leg2, R2.leg2, R3.leg2, R4.leg2
