# Fritzing sketch breadboard_fritz (saved by Fritzing 0.9.4)
breadboards: 1

parts:
  Teensy++1 = Teensy 3.1
  R1 = Rotary Potentiometer (Large) [maximum_resistance=100kΩ package=THT]  # not connected
  R2 = Rotary Potentiometer (Large) [maximum_resistance=100kΩ package=THT]  # not connected
  R3 = Rotary Potentiometer (Large) [maximum_resistance=100kΩ package=THT]  # not connected
  R4 = Rotary Potentiometer (Large) [maximum_resistance=100kΩ package=THT]  # not connected
  S3 = Momentary Switch [package=ksa_sealed_tac_switch]
  S4 = Toggle Switch [package=THT]

nets:
  N1: Teensy++1.AGND, S3.4, S4.L1
