# Fritzing sketch mixer_fritz (saved by Fritzing 1.0.1rc)
perfboards: 1

parts:
  U1 = POT [knob_status=50% power=0.5W part_number=10K package=pot_alpha_rv16af-20]
  R1 = Resistor [tolerance=±5% power=0.25W resistance=10k package=THT]
  U2 = POT [knob_status=50% power=0.5W part_number=10K package=pot_alpha_rv16af-20]
  R2 = Resistor [tolerance=±5% power=0.25W resistance=10k package=THT]
  U3 = POT [knob_status=50% power=0.5W part_number=10K package=pot_alpha_rv16af-20]
  R3 = Resistor [tolerance=±5% power=0.25W resistance=10k package=THT]
  U4 = POT [knob_status=50% power=0.5W part_number=10K package=pot_alpha_rv16af-20]
  R4 = Resistor [tolerance=±5% power=0.25W resistance=10k package=THT]
  U5 = POT [knob_status=50% power=0.5W part_number=10K package=pot_alpha_rv16af-20]
  R5 = Resistor [tolerance=±5% power=0.25W resistance=10k package=THT]
  J8 = Camdenboss CTB0158-2 [part_number=CTB0158-2 package=THT]
  J9 = Camdenboss CTB0158-2 [part_number=CTB0158-2 package=THT]
  J10 = Camdenboss CTB0158-2 [part_number=CTB0158-2 package=THT]
  J11 = Camdenboss CTB0158-2 [part_number=CTB0158-2 package=THT]
  J12 = Camdenboss CTB0158-2 [part_number=CTB0158-2 package=THT]
  J7 = Camdenboss CTB0158-2 [part_number=CTB0158-2 package=THT]

nets:
  N1: U1.A, U2.A, U3.A, U4.A, U5.A, J8.pin1, J9.pin1, J10.pin1, J11.pin1, J12.pin2, J7.pin1
  N2: U1.S, R1.Pin_0
  N3: U1.E, J7.pin2
  N4: R1.Pin_1, R2.Pin_1, R3.Pin_1, R4.Pin_1, R5.Pin_1, J12.pin1
  N5: U2.S, R2.Pin_0
  N6: U2.E, J8.pin2
  N7: U3.S, R3.Pin_0
  N8: U3.E, J9.pin2
  N9: U4.S, R4.Pin_0
  N10: U4.E, J10.pin2
  N11: U5.S, R5.Pin_0
  N12: U5.E, J11.pin2
